# Fritzing sketch sketch (saved by Fritzing 0.9.3b)

parts:
  U1 = NodeMCU V1.0
  J1 = MAGJACK-2 [package=magjack-19938]
  A1 = 2-Channel 5v Relay Shield [package=relay-2ch5v10a]
  TRXCOM1 = RJ45-TRXCOM [part_number=TRJ0011BANL]

nets:
  N1: U1.GND, A1.Pin_10
  N2: U1.D5, A1.Pin_12
  N3: U1.D6, A1.Pin_11
  N4: U1.Vin, A1.Pin_13
  N5: J1.SHIELD, A1.Pin_2
  N6: A1.Pin_1, A1.Pin_4, TRXCOM1.Green_Kathode_-
  N7: A1.Pin_5, TRXCOM1.Yellow_Kathode_-

notes:
  IKEA Rodulf Buttons
  IKEA Rodulf Controller

custom parts:
  NodeMCU V1.0: ESP8266 based NodeMCU
  2-Channel 5v Relay Shield: 2 Channel 5v Relay Shield w. 2x SPD-06VDC-SD-C
